# Fritzing sketch Conexiones_del_Torero (saved by Fritzing 0.9.3b)

parts:
  BT1 = Bluetooth HC-06d [package=THT]
  Componente1 = Arduino Uno (Rev3) - ICSP
  S1 = H-Bridge with L298N
  M1 = DC Motor  # not connected
  M2 = DC Motor
  VCC1 = Battery block 9V
  VCC2 = Battery block 9V  # not connected

nets:
  VCC: BT1.VCC, Componente1.5V
  GND: BT1.GND, Componente1.GND
  N1: BT1.TXD, Componente1.D0/RX
  N2: BT1.RXD, Componente1.D1/TX
  N3: Componente1.D8, S1.IN1
  N4: Componente1.D2, S1.IN4
  N5: Componente1.D4, S1.IN3
  N6: Componente1.D7, S1.IN2
  N7: S1.12V, VCC1.+
  N8: S1.GND, VCC1.-
  N9: S1.OUT4-Motor2, M2.pin_1

notes:
  Bateria de 12 Volts
  Adaptador para Arduino
  Los pins 10 y 6 están unidos a receptores que no se encuentran visibles en este modelo virtual

custom parts:
  Bluetooth HC-06d: Bluetooth HC-06 - face down, pins down 16.5mm x 37.5mm PCB
  H-Bridge with L298N: h-bridge
